# Fritzing sketch arduino_circuit (saved by Fritzing 1.0.6)

parts:
  Bauteil1 = Arduino Nano (Rev3.0) (ICSP)
  S1 = Round Pushbutton
  S2 = Round Pushbutton

nets:
  N1: Bauteil1.GND, S1.leg1, S2.leg1
  N2: Bauteil1.D3, S1.leg0
  N3: Bauteil1.D4, S2.leg0
